# Fritzing sketch System (saved by Fritzing 0.9.3b)
breadboards: 1

parts:
  U1 = GAS_SENSOR [package=mq-3]
  M1 = DC Motor
  Q1 = NPN-Transistor [package="TO92 [THT]"]
  D1 = Zener Diode [part_number=1N4732A breakdown_voltage=3.6V package="Melf DO-213 AB [SMD]"]
  L1 = Solenoid
  J1 = Piezo Speaker
  GSM_SIM_GPSR_SMS_SIM900_SIM1 = SIM800L [package=THT]
  Part1 = Arduino Uno (Rev3) - ICSP
  U2 = LIPO-2000mAh [package=lipo-2000]
  D2 = Zener Diode [part_number=1N4732A breakdown_voltage=3.6V package="Melf DO-213 AB [SMD]"]
  Q2 = NPN-Transistor [package="TO92 [THT]"]
  Part2 = LCD1602-I2C

nets:
  N1: U1.B1, Part1.A0
  5V: U1.H1, Part1.5V, Part2.VCC
  GND: U1.H2, Q1.C, J1.pin1, Part1.GND, U2.-, Q2.C, Part2.GND
  N2: M1.pin_1, Q1.E, D1.cathode
  N3: M1.pin_2, D1.anode, U2.+
  N4: Q1.B, Part1.D2
  N5: L1.pin1, D2.cathode, Q2.E
  N6: L1.pin2, D2.anode
  N7: J1.pin2, Part1.D7
  N8: GSM_SIM_GPSR_SMS_SIM900_SIM1.SIM_TXD, Part1.ICSP_MISO, Part1.D12/MISO
  N9: GSM_SIM_GPSR_SMS_SIM900_SIM1.SIM_RXD, Part1.D11_PWM/MOSI
  N10: Part1.D8, Part2.SDA
  N11: Part1.D9_PWM, Part2.SCL
  N12: Part1.D6_PWM, Q2.B

custom parts:
  LCD1602-I2C: A standard character display, usually with 2x16 characters. Comes in many colors with LCM1602 IIC attached.
